// Logisim project jogo.circ as structural Verilog: 5 circuits, main circuit JOGO
module JOGO (
  input  ligar,
  output out_2,
  output out_3,
  output out_4,
  output out_5,
  output out_6
);

  wire and_1_out, and_2_out, and_3_out, and_4_out, and_5_out, and_6_out, and_7_out, and_8_out, and_9_out,
       and_10_out, and_11_out, and_12_out, and_13_out, and_14_out, and_15_out, and_16_out, and_17_out,
       and_18_out, and_19_out, and_20_out, and_21_out, and_22_out, and_23_out, and_24_out, and_25_out,
       and_26_out, and_27_out, and_28_out, and_29_out, and_30_out, and_31_out, and_32_out, and_33_out,
       and_34_out, and_35_out, and_36_out, and_37_out, and_38_out, and_39_out, and_40_out, and_41_out,
       and_42_out, and_43_out, and_44_out, and_45_out, and_46_out, and_47_out, and_48_out, and_49_out,
       and_50_out, and_51_out, and_52_out, and_53_out, and_54_out, and_55_out, and_56_out, and_57_out,
       and_58_out, and_59_out, and_60_out, and_61_out, and_62_out, and_63_out, and_64_out, and_65_out,
       and_66_out, and_67_out, and_68_out, and_69_out, and_70_out, and_71_out, and_72_out, and_73_out,
       and_74_out, and_75_out, and_76_out, and_77_out, and_78_out, and_79_out, and_80_out, and_81_out,
       and_82_out, and_83_out, and_84_out, and_85_out, and_86_out, and_87_out, and_88_out, and_89_out,
       and_90_out, and_91_out, and_92_out, and_93_out, and_94_out, and_95_out, and_96_out, and_98_out,
       and_99_out, and_100_out, and_103_out, and_105_out, and_106_out, botao1, botao2, clear, clk,
       clock_1_out, demultiplexer_1_out0, demultiplexer_1_out1, entrada1_ON_OFF, loading, multiplexer_1_out,
       multiplexer_2_out, multiplexer_3_out, multiplexer_4_out, multiplexer_5_out, multiplexer_6_out,
       not_1_out, not_2_out, or_1_out, or_2_out, or_3_out, or_4_out, or_5_out, or_6_out, or_24_out,
       or_25_out, pode_atirar, primeiro_clk_16, primeiro_clk_32, shift_up_down_16bits_1_tiro_delay, t_ff_1_q,
       t_ff_2_qn;
  wire [3:0] random_1_out, random_2_out;
  wire [7:0] counter_1_q, counter_2_q;
  wire [15:0] controlled_buffer_1_out, decoder_1_out0, decoder_2_out0, demultiplexer_2_out0,
       demultiplexer_2_out1, L_000, L_001, L_002, L_003, L_004, L_005, L_006, L_007, L_008, L_009, L_010,
       L_011, L_012, L_013, L_014, L_015, L_100, L_101, L_102, L_103, L_104, L_105, L_106, L_107, L_108,
       L_109, L_110, L_111, L_112, L_113, L_114, L_115, multiplexer_7_out, multiplexer_8_out,
       multiplexer_9_out, or_8_out, or_9_out, or_10_out, or_11_out, or_12_out, or_13_out, or_14_out,
       or_15_out, or_16_out, or_17_out, or_18_out, or_19_out, or_20_out, or_21_out, or_22_out, or_23_out,
       or_26_out, R0_00, R0_01, R0_02, R0_03, R0_04, R0_05, R0_06, R0_07, R0_08, R0_09, R0_10, R0_11, R0_12,
       R0_13, R0_14, R0_15, R1_00, R1_01, R1_02, R1_03, R1_04, R1_05, R1_06, R1_07, R1_08, R1_09, R1_10,
       R1_11, R1_12, R1_13, R1_14, R1_15, ram_1_data, rom_1_data, shift_register_1_out, shift_register_2_out,
       shift_register_3_q0, shift_register_3_q1, shift_register_3_q2, shift_register_3_q3,
       shift_register_3_q4, shift_register_3_q5, shift_register_3_q6, shift_register_3_q7,
       shift_register_3_q8, shift_register_3_q9, shift_register_3_q10, shift_register_3_q11,
       shift_register_3_q12, shift_register_3_q13, shift_register_3_q14, shift_register_3_q15;

  Clock clock_1 (.out(clock_1_out));
  and and_1 (and_1_out, R0_05[0], R1_05[0]);
  and and_2 (and_2_out, R0_05[1], R1_05[1]);
  and and_3 (and_3_out, R0_05[2], R1_05[2]);
  and and_4 (and_4_out, R0_05[3], R1_05[3]);
  and and_5 (and_5_out, R0_05[4], R1_05[4]);
  and and_6 (and_6_out, R0_05[5], R1_05[5]);
  and and_7 (and_7_out, R0_05[6], R1_05[6]);
  and and_8 (and_8_out, R0_05[7], R1_05[7]);
  and and_9 (and_9_out, R0_05[8], R1_05[8]);
  and and_10 (and_10_out, R0_05[9], R1_05[9]);
  and and_11 (and_11_out, R0_05[10], R1_05[10]);
  and and_12 (and_12_out, R0_05[11], R1_05[11]);
  and and_13 (and_13_out, R0_05[12], R1_05[12]);
  and and_14 (and_14_out, R0_05[13], R1_05[13]);
  and and_15 (and_15_out, R0_05[14], R1_05[14]);
  and and_16 (and_16_out, R0_05[15], R1_05[15]);
  and and_17 (and_17_out, R0_04[0], R1_04[0]);
  and and_18 (and_18_out, R0_04[1], R1_04[1]);
  and and_19 (and_19_out, R0_04[2], R1_04[2]);
  and and_20 (and_20_out, R0_04[3], R1_04[3]);
  and and_21 (and_21_out, R0_04[4], R1_04[4]);
  and and_22 (and_22_out, R0_04[5], R1_04[5]);
  and and_23 (and_23_out, R0_04[6], R1_04[6]);
  and and_24 (and_24_out, R0_04[7], R1_04[7]);
  and and_25 (and_25_out, R0_04[8], R1_04[8]);
  and and_26 (and_26_out, R0_04[9], R1_04[9]);
  and and_27 (and_27_out, R0_04[10], R1_04[10]);
  and and_28 (and_28_out, R0_04[11], R1_04[11]);
  and and_29 (and_29_out, R0_04[12], R1_04[12]);
  and and_30 (and_30_out, R0_04[13], R1_04[13]);
  and and_31 (and_31_out, R0_04[14], R1_04[14]);
  and and_32 (and_32_out, R0_04[15], R1_04[15]);
  and and_33 (and_33_out, R0_03[0], R1_03[0]);
  and and_34 (and_34_out, R0_03[1], R1_03[1]);
  and and_35 (and_35_out, R0_03[2], R1_03[2]);
  and and_36 (and_36_out, R0_03[3], R1_03[3]);
  and and_37 (and_37_out, R0_03[4], R1_03[4]);
  and and_38 (and_38_out, R0_03[5], R1_03[5]);
  and and_39 (and_39_out, R0_03[6], R1_03[6]);
  and and_40 (and_40_out, R0_03[7], R1_03[7]);
  and and_41 (and_41_out, R0_03[8], R1_03[8]);
  and and_42 (and_42_out, R0_03[9], R1_03[9]);
  and and_43 (and_43_out, R0_03[10], R1_03[10]);
  and and_44 (and_44_out, R0_03[11], R1_03[11]);
  and and_45 (and_45_out, R0_03[12], R1_03[12]);
  and and_46 (and_46_out, R0_03[13], R1_03[13]);
  and and_47 (and_47_out, R0_03[14], R1_03[14]);
  and and_48 (and_48_out, R0_03[15], R1_03[15]);
  and and_49 (and_49_out, R0_02[0], R1_02[0]);
  and and_50 (and_50_out, R0_02[1], R1_02[1]);
  and and_51 (and_51_out, R0_02[2], R1_02[2]);
  and and_52 (and_52_out, R0_02[3], R1_02[3]);
  and and_53 (and_53_out, R0_02[4], R1_02[4]);
  and and_54 (and_54_out, R0_02[5], R1_02[5]);
  and and_55 (and_55_out, R0_02[6], R1_02[6]);
  and and_56 (and_56_out, R0_02[7], R1_02[7]);
  and and_57 (and_57_out, R0_02[8], R1_02[8]);
  and and_58 (and_58_out, R0_02[9], R1_02[9]);
  and and_59 (and_59_out, R0_02[10], R1_02[10]);
  and and_60 (and_60_out, R0_02[11], R1_02[11]);
  and and_61 (and_61_out, R0_02[12], R1_02[12]);
  and and_62 (and_62_out, R0_02[13], R1_02[13]);
  and and_63 (and_63_out, R0_02[14], R1_02[14]);
  and and_64 (and_64_out, R0_02[15], R1_02[15]);
  and and_65 (and_65_out, R0_01[0], R1_01[0]);
  and and_66 (and_66_out, R0_01[1], R1_01[1]);
  and and_67 (and_67_out, R0_01[2], R1_01[2]);
  and and_68 (and_68_out, R0_01[3], R1_01[3]);
  and and_69 (and_69_out, R0_01[4], R1_01[4]);
  and and_70 (and_70_out, R0_01[5], R1_01[5]);
  and and_71 (and_71_out, R0_01[6], R1_01[6]);
  and and_72 (and_72_out, R0_01[7], R1_01[7]);
  and and_73 (and_73_out, R0_01[8], R1_01[8]);
  and and_74 (and_74_out, R0_01[9], R1_01[9]);
  and and_75 (and_75_out, R0_01[10], R1_01[10]);
  and and_76 (and_76_out, R0_01[11], R1_01[11]);
  and and_77 (and_77_out, R0_01[12], R1_01[12]);
  and and_78 (and_78_out, R0_01[13], R1_01[13]);
  and and_79 (and_79_out, R0_01[14], R1_01[14]);
  and and_80 (and_80_out, R0_01[15], R1_01[15]);
  and and_81 (and_81_out, R0_00[0], R1_00[0]);
  and and_82 (and_82_out, R0_00[1], R1_00[1]);
  and and_83 (and_83_out, R0_00[2], R1_00[2]);
  and and_84 (and_84_out, R0_00[3], R1_00[3]);
  and and_85 (and_85_out, R0_00[4], R1_00[4]);
  and and_86 (and_86_out, R0_00[5], R1_00[5]);
  and and_87 (and_87_out, R0_00[6], R1_00[6]);
  and and_88 (and_88_out, R0_00[7], R1_00[7]);
  and and_89 (and_89_out, R0_00[8], R1_00[8]);
  and and_90 (and_90_out, R0_00[9], R1_00[9]);
  and and_91 (and_91_out, R0_00[10], R1_00[10]);
  and and_92 (and_92_out, R0_00[11], R1_00[11]);
  and and_93 (and_93_out, R0_00[12], R1_00[12]);
  and and_94 (and_94_out, R0_00[13], R1_00[13]);
  and and_95 (and_95_out, R0_00[14], R1_00[14]);
  and and_96 (and_96_out, R0_00[15], R1_00[15]);
  and and_97 (clk, clock_1_out, ~out_2, ligar);  // AND_Gate
  or or_1 (or_1_out, and_1_out, and_2_out, and_3_out, and_4_out, and_5_out, and_6_out, and_7_out, and_8_out, and_9_out, and_10_out, and_11_out, and_12_out, and_13_out, and_14_out, and_15_out, and_16_out);
  or or_2 (or_2_out, and_17_out, and_18_out, and_19_out, and_20_out, and_21_out, and_22_out, and_23_out, and_24_out, and_25_out, and_26_out, and_27_out, and_28_out, and_29_out, and_30_out, and_31_out, and_32_out);
  or or_3 (or_3_out, and_33_out, and_34_out, and_35_out, and_36_out, and_37_out, and_38_out, and_39_out, and_40_out, and_41_out, and_42_out, and_43_out, and_44_out, and_45_out, and_46_out, and_47_out, and_48_out);
  or or_4 (or_4_out, and_49_out, and_50_out, and_51_out, and_52_out, and_53_out, and_54_out, and_55_out, and_56_out, and_57_out, and_58_out, and_59_out, and_60_out, and_61_out, and_62_out, and_63_out, and_64_out);
  or or_5 (or_5_out, and_65_out, and_66_out, and_67_out, and_68_out, and_69_out, and_70_out, and_71_out, and_72_out, and_73_out, and_74_out, and_75_out, and_76_out, and_77_out, and_78_out, and_79_out, and_80_out);
  or or_6 (or_6_out, and_81_out, and_82_out, and_83_out, and_84_out, and_85_out, and_86_out, and_87_out, and_88_out, and_89_out, and_90_out, and_91_out, and_92_out, and_93_out, and_94_out, and_95_out, and_96_out);
  T_Flip_Flop t_ff_1 (.clk(out_4), .T(1'b1), .Q(t_ff_1_q));  // open: Qn, preset, reset, en
  Shift_Register #(.width(16), .length(16), .trigger("falling")) shift_register_1 (
    .shift(t_ff_1_q), .clk(clk), .out(shift_register_1_out), .load(out_6), .d0(R0_15), .d1(R0_14),
    .d2(R0_13), .d3(R0_12), .d4(R0_11), .d5(R0_10), .d6(R0_09), .d7(R0_08), .d8(R0_07), .d9(R0_06),
    .d10(R0_05), .d11(R0_04), .d12(R0_03), .d13(R0_02), .d14(R0_01), .d15(R0_00));  // open: in, clr, q0, q1, q2, q3, q4, q5, q6, q7, q8, q9, q10, q11, q12, q13, q14, q15
  Multiplexer multiplexer_1 (.in0(1'b0), .in1(or_1_out), .out(multiplexer_1_out), .sel(out_4));  // open: en
  Multiplexer multiplexer_2 (.in0(1'b0), .in1(or_2_out), .out(multiplexer_2_out), .sel(out_4));  // open: en
  Multiplexer multiplexer_3 (.in0(1'b0), .in1(or_3_out), .out(multiplexer_3_out), .sel(out_4));  // open: en
  Multiplexer multiplexer_4 (.in0(1'b0), .in1(or_4_out), .out(multiplexer_4_out), .sel(out_4));  // open: en
  Multiplexer multiplexer_5 (.in0(1'b0), .in1(or_5_out), .out(multiplexer_5_out), .sel(out_4));  // open: en
  Multiplexer multiplexer_6 (.in0(1'b0), .in1(or_6_out), .out(multiplexer_6_out), .sel(out_4));  // open: en
  Counter #(.max('h1f), .ongoal("stay")) counter_1 (
    .Q(counter_1_q), .carry(loading), .clk(and_98_out));  // open: load, D, count, clr
  and and_98 (and_98_out, clk, ligar);
  T_Flip_Flop t_ff_2 (.clk(out_4), .T(1'b1), .Qn(t_ff_2_qn));  // open: Q, preset, reset, en
  Shift_Register #(.width(16), .length(16)) shift_register_2 (
    .shift(t_ff_2_qn), .clk(clk), .out(shift_register_2_out), .load(out_6), .d0(R1_15), .d1(R1_14),
    .d2(R1_13), .d3(R1_12), .d4(R1_11), .d5(R1_10), .d6(R1_09), .d7(R1_08), .d8(R1_07), .d9(R1_06),
    .d10(R1_05), .d11(R1_04), .d12(R1_03), .d13(R1_02), .d14(R1_01), .d15(R1_00));  // open: in, clr, q0, q1, q2, q3, q4, q5, q6, q7, q8, q9, q10, q11, q12, q13, q14, q15
  ROM #(.dataWidth(16)) rom_1 (.addr(counter_1_q), .data(rom_1_data));  // open: sel
  or or_7 (out_2, multiplexer_1_out, multiplexer_2_out, multiplexer_3_out, multiplexer_4_out, multiplexer_5_out, multiplexer_6_out);
  assign or_8_out = R0_15 | R1_15;  // OR_Gate or_8, 16 bits wide
  assign or_9_out = R0_14 | R1_14;  // OR_Gate or_9, 16 bits wide
  assign or_10_out = R0_13 | R1_13;  // OR_Gate or_10, 16 bits wide
  assign or_11_out = R0_12 | R1_12;  // OR_Gate or_11, 16 bits wide
  assign or_12_out = R0_11 | R1_11;  // OR_Gate or_12, 16 bits wide
  assign or_13_out = R0_10 | R1_10;  // OR_Gate or_13, 16 bits wide
  assign or_14_out = R0_09 | R1_09;  // OR_Gate or_14, 16 bits wide
  assign or_15_out = R0_08 | R1_08;  // OR_Gate or_15, 16 bits wide
  assign or_16_out = R0_07 | R1_07;  // OR_Gate or_16, 16 bits wide
  assign or_17_out = R0_06 | R1_06;  // OR_Gate or_17, 16 bits wide
  assign or_18_out = R0_05 | R1_05;  // OR_Gate or_18, 16 bits wide
  assign or_19_out = R0_04 | R1_04;  // OR_Gate or_19, 16 bits wide
  assign or_20_out = R0_03 | R1_03;  // OR_Gate or_20, 16 bits wide
  assign or_21_out = R0_02 | R1_02;  // OR_Gate or_21, 16 bits wide
  assign or_22_out = R0_01 | R1_01;  // OR_Gate or_22, 16 bits wide
  assign or_23_out = R0_00 | R1_00;  // OR_Gate or_23, 16 bits wide
  Multiplexer #(.width(16)) multiplexer_7 (
    .in0(shift_register_2_out), .in1(shift_register_1_out), .out(multiplexer_7_out), .sel(out_5));  // open: en
  and and_99 (and_99_out, loading, primeiro_clk_32);
  Shift_Register #(.width(16), .length(16)) shift_register_3 (
    .shift(1'b0), .clk(out_6), .load(1'b1), .d0(or_23_out), .q0(shift_register_3_q0), .d1(or_22_out),
    .q1(shift_register_3_q1), .d2(or_21_out), .q2(shift_register_3_q2), .d3(or_20_out),
    .q3(shift_register_3_q3), .d4(or_19_out), .q4(shift_register_3_q4), .d5(or_18_out),
    .q5(shift_register_3_q5), .d6(or_17_out), .q6(shift_register_3_q6), .d7(or_16_out),
    .q7(shift_register_3_q7), .d8(or_15_out), .q8(shift_register_3_q8), .d9(or_14_out),
    .q9(shift_register_3_q9), .d10(or_13_out), .q10(shift_register_3_q10), .d11(or_12_out),
    .q11(shift_register_3_q11), .d12(or_11_out), .q12(shift_register_3_q12), .d13(or_10_out),
    .q13(shift_register_3_q13), .d14(or_9_out), .q14(shift_register_3_q14), .d15(or_8_out),
    .q15(shift_register_3_q15));  // open: in, out, clr
  assign controlled_buffer_1_out = not_1_out ? rom_1_data : 16'bz;  // Controlled_Buffer controlled_buffer_1
  not not_1 (not_1_out, and_99_out);
  Multiplexer #(.width(16)) multiplexer_8 (
    .in0(multiplexer_7_out), .in1(controlled_buffer_1_out), .out(multiplexer_8_out), .sel(not_1_out));  // open: en
  Counter #(.max('h21), .trigger("falling")) counter_2 (
    .Q(counter_2_q), .clk(clk), .clr(out_3));  // open: load, D, count, carry
  DotMatrix #(.inputtype("row"), .matrixcols(16), .matrixrows(16)) dotmatrix_1 (
    .row0(shift_register_3_q15), .row1(shift_register_3_q14), .row2(shift_register_3_q13),
    .row3(shift_register_3_q12), .row4(shift_register_3_q11), .row5(shift_register_3_q10),
    .row6(shift_register_3_q9), .row7(shift_register_3_q8), .row8(shift_register_3_q7),
    .row9(shift_register_3_q6), .row10(shift_register_3_q5), .row11(shift_register_3_q4),
    .row12(shift_register_3_q3), .row13(shift_register_3_q2), .row14(shift_register_3_q1),
    .row15(shift_register_3_q0));
  Button button_1 (.out(botao1));
  Button button_2 (.out(botao2));
  and and_100 (and_100_out, ~counter_2_q[0], ~counter_2_q[1], ~counter_2_q[2], ~counter_2_q[3], ~counter_2_q[4], ~counter_2_q[5], ~counter_2_q[6], ~counter_2_q[7]);  // AND_Gate
  and and_101 (out_4, ~counter_2_q[0], ~counter_2_q[1], ~counter_2_q[2], ~counter_2_q[3], counter_2_q[4], ~counter_2_q[5], ~counter_2_q[6], ~counter_2_q[7]);  // AND_Gate
  and and_102 (out_3, ~counter_2_q[0], ~counter_2_q[1], ~counter_2_q[2], ~counter_2_q[3], ~counter_2_q[4], counter_2_q[5], ~counter_2_q[6], ~counter_2_q[7]);  // AND_Gate
  and and_103 (and_103_out, ~counter_2_q[0], counter_2_q[1], ~counter_2_q[2], ~counter_2_q[3], counter_2_q[4], ~counter_2_q[5], ~counter_2_q[6], ~counter_2_q[7]);  // AND_Gate
  and and_104 (clear, counter_2_q[0], ~counter_2_q[1], ~counter_2_q[2], ~counter_2_q[3], ~counter_2_q[4], counter_2_q[5], ~counter_2_q[6], ~counter_2_q[7]);  // AND_Gate
  not not_2 (not_2_out, out_6);
  T_Flip_Flop t_ff_3 (.clk(and_100_out), .T(1'b1), .Q(out_6));  // open: Qn, preset, reset, en
  RAM #(.dataWidth(16), .bus("separate")) ram_1 (
    .addr(counter_2_q), .din(multiplexer_8_out), .data(ram_1_data), .str(not_2_out), .clk(clk), .ld(out_6));  // open: sel, clr
  or or_24 (or_24_out, out_4, out_3);
  or or_25 (or_25_out, and_103_out, clear);
  T_Flip_Flop t_ff_4 (.clk(or_24_out), .T(1'b1), .Q(out_5));  // open: Qn, preset, reset, en
  T_Flip_Flop t_ff_5 (.clk(or_25_out), .T(1'b1), .Q(entrada1_ON_OFF));  // open: Qn, preset, reset, en
  and and_105 (and_105_out, clk, out_6);
  Demultiplexer demultiplexer_1 (
    .out0(demultiplexer_1_out0), .out1(demultiplexer_1_out1), .in(and_105_out), .sel(out_5));  // open: en
  Demultiplexer #(.width(16)) demultiplexer_2 (
    .out0(demultiplexer_2_out0), .out1(demultiplexer_2_out1), .in(ram_1_data), .sel(out_5));  // open: en
  D_Flip_Flop d_ff_1 (.Q(primeiro_clk_16), .preset(out_4));  // open: clk, D, Qn, en, reset
  D_Flip_Flop d_ff_2 (.Q(primeiro_clk_32), .preset(out_3));  // open: clk, D, Qn, en, reset
  Decoder #(.select(4)) decoder_1 (
    .out0(decoder_1_out0[0]), .out1(decoder_1_out0[1]), .out2(decoder_1_out0[2]), .out3(decoder_1_out0[3]),
    .out4(decoder_1_out0[4]), .out5(decoder_1_out0[5]), .out6(decoder_1_out0[6]), .out7(decoder_1_out0[7]),
    .out8(decoder_1_out0[8]), .out9(decoder_1_out0[9]), .out10(decoder_1_out0[10]),
    .out11(decoder_1_out0[11]), .out12(decoder_1_out0[12]), .out13(decoder_1_out0[13]),
    .out14(decoder_1_out0[14]), .out15(decoder_1_out0[15]), .sel(random_1_out));  // open: en
  Random #(.width(4), .seed(91745)) random_1 (.clk(pode_atirar), .out(random_1_out));  // open: next, clr
  assign or_26_out = decoder_1_out0 | decoder_2_out0;  // OR_Gate or_26, 16 bits wide
  Decoder #(.select(4)) decoder_2 (
    .out0(decoder_2_out0[0]), .out1(decoder_2_out0[1]), .out2(decoder_2_out0[2]), .out3(decoder_2_out0[3]),
    .out4(decoder_2_out0[4]), .out5(decoder_2_out0[5]), .out6(decoder_2_out0[6]), .out7(decoder_2_out0[7]),
    .out8(decoder_2_out0[8]), .out9(decoder_2_out0[9]), .out10(decoder_2_out0[10]),
    .out11(decoder_2_out0[11]), .out12(decoder_2_out0[12]), .out13(decoder_2_out0[13]),
    .out14(decoder_2_out0[14]), .out15(decoder_2_out0[15]), .sel(random_2_out));  // open: en
  Random #(.width(4), .seed(5491276)) random_2 (.clk(pode_atirar), .out(random_2_out));  // open: next, clr
  Shift_Register #(.width(16), .length(16)) shift_register_4 (
    .in(demultiplexer_2_out0), .clk(demultiplexer_1_out0), .q0(L_015), .q1(L_014), .q2(L_013), .q3(L_012),
    .q4(L_011), .q5(L_010), .q6(L_009), .q7(L_008), .q8(L_007), .q9(L_006), .q10(L_005), .q11(L_004),
    .q12(L_003), .q13(L_002), .q14(L_001), .q15(L_000));  // open: shift, out, load, clr, d0, d1, d2, d3, d4, d5, d6, d7, d8, d9, d10, d11, d12, d13, d14, d15
  Shift_Register #(.width(16), .length(16)) shift_register_5 (
    .in(demultiplexer_2_out1), .clk(demultiplexer_1_out1), .q0(L_115), .q1(L_114), .q2(L_113), .q3(L_112),
    .q4(L_111), .q5(L_110), .q6(L_109), .q7(L_108), .q8(L_107), .q9(L_106), .q10(L_105), .q11(L_104),
    .q12(L_103), .q13(L_102), .q14(L_101), .q15(L_100));  // open: shift, out, load, clr, d0, d1, d2, d3, d4, d5, d6, d7, d8, d9, d10, d11, d12, d13, d14, d15
  Multiplexer #(.width(16)) multiplexer_9 (
    .in0(L_115), .in1(or_26_out), .out(multiplexer_9_out), .sel(pode_atirar));  // open: en
  shift_Up_Down_16BITS shift_up_down_16bits_1 (
    ._00(L_100), ._01(L_101), ._02(L_102), ._03(L_103), ._04(L_104), ._05(L_105), ._06(L_106), ._07(L_107),
    ._08(L_108), ._09(L_109), ._10(L_110), ._11(L_111), ._12(L_112), ._13(L_113), ._14(L_114),
    ._15(multiplexer_9_out), .clk(out_6), .S_15(R0_15), .S_14(R0_14), .S_13(R0_13), .S_12(R0_12),
    .S_10(R0_10), .S_09(R0_09), .S_08(R0_08), .S_11(R0_11), .S_06(R0_06), .S_05(R0_05), .S_04(R0_04),
    .S_03(R0_03), .S_02(R0_02), .S_01(R0_01), .S_00(R0_00), .S_07(R0_07),
    .tiro_delay(shift_up_down_16bits_1_tiro_delay));
  Counter #(.max('h8)) counter_3 (
    .carry(pode_atirar), .clk(shift_up_down_16bits_1_tiro_delay), .clr(and_106_out));  // open: load, D, count, Q
  and and_106 (and_106_out, pode_atirar, ~out_6);  // AND_Gate
  shift_Left_Right_16BITS shift_left_right_16bits_1 (
    .botao1(botao1), .botao2(botao2), .L_015(R1_15), .L_007(R1_07), .L_014(R1_14), .L_006(R1_06),
    .L_013(R1_13), .L_005(R1_05), .L_012(R1_12), .L_004(R1_04), .L_011(R1_11), .L_003(R1_03), .L_010(R1_10),
    .L_002(R1_02), .L_009(R1_09), .L_001(R1_01), .L_008(R1_08), .L_000(R1_00), ._01(L_001), ._02(L_002),
    ._03(L_003), ._04(L_004), ._05(L_005), ._06(L_006), ._07(L_007), ._08(L_008), ._09(L_009), ._10(L_010),
    ._11(L_011), ._12(L_012), ._13(L_013), ._14(L_014), ._15(L_015), ._00(L_000));

  // Other names for the same wires on the sheet: clk_16 = out_4; clk_32 = out_3; E_S = out_6; perdeu = out_2;
  //   rota = out_5

  // Notes on the sheet:
  //   ROM
  //   contents of rom_1 (hex, n*v repeats v):
  //   0 1c0 80 80 3e0 80
endmodule

module decod_BIN8BITSxDEC16BITS (
  input  a,
  input  b,
  input  c,
  input  d,
  input  e,
  input  f,
  input  g,
  input  h,
  input  i,
  input  j,
  input  k,
  input  l,
  input  m,
  input  n,
  input  o,
  input  p
);

  wire a_prime, b_prime, c_prime, d_prime, e_prime, f_prime, g_prime, h_prime, i_prime, j_prime, k_prime,
       l_prime, m_prime, n_prime, o_prime, p_prime, q0, q1;

  not not_1 (a_prime, a);
  not not_2 (b_prime, b);
  not not_3 (c_prime, c);
  not not_4 (d_prime, d);
  not not_5 (e_prime, e);
  not not_6 (f_prime, f);
  not not_7 (g_prime, g);
  not not_8 (h_prime, h);
  not not_9 (i_prime, i);
  not not_10 (j_prime, j);
  not not_11 (k_prime, k);
  not not_12 (l_prime, l);
  not not_13 (m_prime, m);
  not not_14 (n_prime, n);
  not not_15 (o_prime, o);
  not not_16 (p_prime, p);
  and and_1 (q0, a_prime, b_prime, c_prime, d_prime, e_prime, f_prime, g_prime, h_prime, i_prime, j_prime, k_prime, l_prime, m_prime, n_prime, o_prime, p_prime);
  and and_2 (q1, a, b_prime, c_prime, d_prime, e_prime, f_prime, g_prime, h_prime, i_prime, j_prime, k_prime, l_prime, m_prime, n_prime, o_prime, p_prime);
endmodule

module backup (
  input  ligar,
  output out_2,
  output out_3,
  output out_4,
  output out_5,
  output out_6
);

  wire and_2_out, and_3_out, and_4_out, and_5_out, and_6_out, and_7_out, and_8_out, and_9_out, and_10_out,
       and_11_out, and_12_out, and_13_out, and_14_out, and_15_out, and_16_out, and_17_out, and_18_out,
       and_19_out, and_20_out, and_21_out, and_22_out, and_23_out, and_24_out, and_25_out, and_26_out,
       and_27_out, and_28_out, and_29_out, and_30_out, and_31_out, and_32_out, and_33_out, and_34_out,
       and_35_out, and_36_out, and_37_out, and_38_out, and_39_out, and_40_out, and_41_out, and_42_out,
       and_43_out, and_44_out, and_45_out, and_46_out, and_47_out, and_48_out, and_49_out, and_50_out,
       and_51_out, and_52_out, and_53_out, and_54_out, and_55_out, and_56_out, and_57_out, and_58_out,
       and_59_out, and_60_out, and_61_out, and_62_out, and_63_out, and_64_out, and_65_out, and_66_out,
       and_67_out, and_68_out, and_69_out, and_70_out, and_71_out, and_72_out, and_73_out, and_74_out,
       and_75_out, and_76_out, and_77_out, and_78_out, and_79_out, and_80_out, and_81_out, and_82_out,
       and_83_out, and_84_out, and_85_out, and_86_out, and_87_out, and_88_out, and_89_out, and_90_out,
       and_91_out, and_92_out, and_93_out, and_94_out, and_95_out, and_96_out, and_97_out, and_98_out,
       and_99_out, and_100_out, and_103_out, and_105_out, and_106_out, botao1, botao2, clear, clk,
       clock_1_out, demultiplexer_1_out0, demultiplexer_1_out1, entrada1_ON_OFF, loading, multiplexer_3_out,
       multiplexer_4_out, multiplexer_5_out, multiplexer_6_out, multiplexer_7_out, multiplexer_8_out,
       not_1_out, not_2_out, or_17_out, or_18_out, or_19_out, or_20_out, or_21_out, or_22_out, or_23_out,
       or_24_out, pode_atirar, primeiro_clk_16, primeiro_clk_32, shift_up_down_16bits_1_tiro_delay, t_ff_1_q,
       t_ff_2_qn;
  wire [3:0] random_1_out, random_2_out;
  wire [7:0] counter_1_q, counter_2_q;
  wire [15:0] controlled_buffer_1_out, decoder_1_out0, decoder_2_out0, demultiplexer_2_out0,
       demultiplexer_2_out1, L_000, L_001, L_002, L_003, L_004, L_005, L_006, L_007, L_008, L_009, L_010,
       L_011, L_012, L_013, L_014, L_015, L_100, L_101, L_102, L_103, L_104, L_105, L_106, L_107, L_108,
       L_109, L_110, L_111, L_112, L_113, L_114, L_115, multiplexer_1_out, multiplexer_2_out,
       multiplexer_9_out, or_1_out, or_2_out, or_3_out, or_4_out, or_5_out, or_6_out, or_7_out, or_8_out,
       or_9_out, or_10_out, or_11_out, or_12_out, or_13_out, or_14_out, or_15_out, or_16_out, or_26_out,
       R0_00, R0_01, R0_02, R0_03, R0_04, R0_05, R0_06, R0_07, R0_08, R0_09, R0_10, R0_11, R0_12, R0_13,
       R0_14, R0_15, R1_00, R1_01, R1_02, R1_03, R1_04, R1_05, R1_06, R1_07, R1_08, R1_09, R1_10, R1_11,
       R1_12, R1_13, R1_14, R1_15, ram_1_data, rom_1_data, shift_register_1_out, shift_register_1_q0,
       shift_register_1_q1, shift_register_1_q2, shift_register_1_q3, shift_register_1_q4,
       shift_register_1_q5, shift_register_1_q6, shift_register_1_q7, shift_register_1_q8,
       shift_register_1_q9, shift_register_1_q10, shift_register_1_q11, shift_register_1_q12,
       shift_register_1_q13, shift_register_1_q14, shift_register_1_q15, shift_register_2_q0,
       shift_register_2_q1, shift_register_2_q2, shift_register_2_q3, shift_register_2_q4,
       shift_register_2_q5, shift_register_2_q6, shift_register_2_q7, shift_register_2_q8,
       shift_register_2_q9, shift_register_2_q10, shift_register_2_q11, shift_register_2_q12,
       shift_register_2_q13, shift_register_2_q14, shift_register_2_q15, shift_register_3_out,
       shift_register_3_q0, shift_register_3_q1, shift_register_3_q2, shift_register_3_q3,
       shift_register_3_q4, shift_register_3_q5, shift_register_3_q6, shift_register_3_q7,
       shift_register_3_q8, shift_register_3_q9, shift_register_3_q10, shift_register_3_q11,
       shift_register_3_q12, shift_register_3_q13, shift_register_3_q14, shift_register_3_q15, undriven;

  Clock clock_1 (.out(clock_1_out));
  and and_1 (clk, clock_1_out, ~out_2, ligar);  // AND_Gate
  T_Flip_Flop t_ff_1 (.clk(out_4), .T(1'b1), .Q(t_ff_1_q));  // open: Qn, preset, reset, en
  Shift_Register #(.width(16), .length(16), .trigger("falling")) shift_register_1 (
    .shift(t_ff_1_q), .clk(clk), .out(shift_register_1_out), .load(out_6), .d0(R0_15),
    .q0(shift_register_1_q0), .d1(R0_14), .q1(shift_register_1_q1), .d2(R0_13), .q2(shift_register_1_q2),
    .d3(R0_12), .q3(shift_register_1_q3), .d4(R0_11), .q4(shift_register_1_q4), .d5(R0_10),
    .q5(shift_register_1_q5), .d6(R0_09), .q6(shift_register_1_q6), .d7(R0_08), .q7(shift_register_1_q7),
    .d8(R0_07), .q8(shift_register_1_q8), .d9(R0_06), .q9(shift_register_1_q9), .d10(R0_05),
    .q10(shift_register_1_q10), .d11(R0_04), .q11(shift_register_1_q11), .d12(R0_03),
    .q12(shift_register_1_q12), .d13(R0_02), .q13(shift_register_1_q13), .d14(R0_01),
    .q14(shift_register_1_q14), .d15(R0_00), .q15(shift_register_1_q15));  // open: in, clr
  // Probe on shift_register_1_q0
  // Probe on shift_register_1_q1
  // Probe on shift_register_1_q2
  // Probe on shift_register_1_q3
  // Probe on shift_register_1_q4
  // Probe on shift_register_1_q5
  // Probe on shift_register_1_q6
  // Probe on shift_register_1_q7
  // Probe on shift_register_1_q8
  // Probe on shift_register_1_q9
  // Probe on shift_register_1_q10
  // Probe on shift_register_1_q11
  // Probe on shift_register_1_q12
  // Probe on shift_register_1_q13
  // Probe on shift_register_1_q14
  // Probe on shift_register_1_q15
  Counter #(.max('h1f), .ongoal("stay")) counter_1 (
    .Q(counter_1_q), .carry(loading), .clk(and_2_out));  // open: load, D, count, clr
  and and_2 (and_2_out, clk, ligar);
  assign or_1_out = R0_15 | R1_15;  // OR_Gate or_1, 16 bits wide
  assign or_2_out = R0_14 | R1_14;  // OR_Gate or_2, 16 bits wide
  assign or_3_out = R0_13 | R1_13;  // OR_Gate or_3, 16 bits wide
  assign or_4_out = R0_12 | R1_12;  // OR_Gate or_4, 16 bits wide
  assign or_5_out = R0_11 | R1_11;  // OR_Gate or_5, 16 bits wide
  assign or_6_out = R0_10 | R1_10;  // OR_Gate or_6, 16 bits wide
  assign or_7_out = R0_09 | R1_09;  // OR_Gate or_7, 16 bits wide
  assign or_8_out = R0_08 | R1_08;  // OR_Gate or_8, 16 bits wide
  assign or_9_out = R0_07 | R1_07;  // OR_Gate or_9, 16 bits wide
  assign or_10_out = R0_06 | R1_06;  // OR_Gate or_10, 16 bits wide
  assign or_11_out = R0_05 | R1_05;  // OR_Gate or_11, 16 bits wide
  assign or_12_out = R0_04 | R1_04;  // OR_Gate or_12, 16 bits wide
  assign or_13_out = R0_03 | R1_03;  // OR_Gate or_13, 16 bits wide
  assign or_14_out = R0_02 | R1_02;  // OR_Gate or_14, 16 bits wide
  assign or_15_out = R0_01 | R1_01;  // OR_Gate or_15, 16 bits wide
  assign or_16_out = R0_00 | R1_00;  // OR_Gate or_16, 16 bits wide
  T_Flip_Flop t_ff_2 (.clk(out_4), .T(1'b1), .Qn(t_ff_2_qn));  // open: Q, preset, reset, en
  Shift_Register #(.width(16), .length(16)) shift_register_2 (
    .shift(1'b0), .clk(out_6), .load(1'b1), .d0(or_16_out), .q0(shift_register_2_q0), .d1(or_15_out),
    .q1(shift_register_2_q1), .d2(or_14_out), .q2(shift_register_2_q2), .d3(or_13_out),
    .q3(shift_register_2_q3), .d4(or_12_out), .q4(shift_register_2_q4), .d5(or_11_out),
    .q5(shift_register_2_q5), .d6(or_10_out), .q6(shift_register_2_q6), .d7(or_9_out),
    .q7(shift_register_2_q7), .d8(or_8_out), .q8(shift_register_2_q8), .d9(or_7_out),
    .q9(shift_register_2_q9), .d10(or_6_out), .q10(shift_register_2_q10), .d11(or_5_out),
    .q11(shift_register_2_q11), .d12(or_4_out), .q12(shift_register_2_q12), .d13(or_3_out),
    .q13(shift_register_2_q13), .d14(or_2_out), .q14(shift_register_2_q14), .d15(or_1_out),
    .q15(shift_register_2_q15));  // open: in, out, clr
  Shift_Register #(.width(16), .length(16)) shift_register_3 (
    .shift(t_ff_2_qn), .clk(clk), .out(shift_register_3_out), .load(out_6), .d0(R1_15),
    .q0(shift_register_3_q0), .d1(R1_14), .q1(shift_register_3_q1), .d2(R1_13), .q2(shift_register_3_q2),
    .d3(R1_12), .q3(shift_register_3_q3), .d4(R1_11), .q4(shift_register_3_q4), .d5(R1_10),
    .q5(shift_register_3_q5), .d6(R1_09), .q6(shift_register_3_q6), .d7(R1_08), .q7(shift_register_3_q7),
    .d8(R1_07), .q8(shift_register_3_q8), .d9(R1_06), .q9(shift_register_3_q9), .d10(R1_05),
    .q10(shift_register_3_q10), .d11(R1_04), .q11(shift_register_3_q11), .d12(R1_03),
    .q12(shift_register_3_q12), .d13(R1_02), .q13(shift_register_3_q13), .d14(R1_01),
    .q14(shift_register_3_q14), .d15(R1_00), .q15(shift_register_3_q15));  // open: in, clr
  // Probe on shift_register_3_q0
  // Probe on shift_register_3_q1
  // Probe on shift_register_3_q2
  // Probe on shift_register_3_q3
  // Probe on shift_register_3_q4
  // Probe on shift_register_3_q5
  // Probe on shift_register_3_q6
  // Probe on shift_register_3_q7
  // Probe on shift_register_3_q8
  // Probe on shift_register_3_q9
  // Probe on shift_register_3_q10
  // Probe on shift_register_3_q11
  // Probe on shift_register_3_q12
  // Probe on shift_register_3_q13
  // Probe on shift_register_3_q14
  // Probe on shift_register_3_q15
  ROM #(.dataWidth(16)) rom_1 (.addr(counter_1_q), .data(rom_1_data));  // open: sel
  and and_3 (and_3_out, R0_05[0], R1_05[0]);
  and and_4 (and_4_out, R0_05[1], R1_05[1]);
  and and_5 (and_5_out, R0_05[2], R1_05[2]);
  and and_6 (and_6_out, R0_05[3], R1_05[3]);
  and and_7 (and_7_out, R0_05[4], R1_05[4]);
  and and_8 (and_8_out, R0_05[5], R1_05[5]);
  and and_9 (and_9_out, R0_05[6], R1_05[6]);
  and and_10 (and_10_out, R0_05[7], R1_05[7]);
  and and_11 (and_11_out, R0_05[8], R1_05[8]);
  and and_12 (and_12_out, R0_05[9], R1_05[9]);
  and and_13 (and_13_out, R0_05[10], R1_05[10]);
  and and_14 (and_14_out, R0_05[11], R1_05[11]);
  and and_15 (and_15_out, R0_05[12], R1_05[12]);
  and and_16 (and_16_out, R0_05[13], R1_05[13]);
  and and_17 (and_17_out, R0_05[14], R1_05[14]);
  and and_18 (and_18_out, R0_05[15], R1_05[15]);
  and and_19 (and_19_out, R0_04[0], R1_04[0]);
  and and_20 (and_20_out, R0_04[1], R1_04[1]);
  and and_21 (and_21_out, R0_04[2], R1_04[2]);
  and and_22 (and_22_out, R0_04[3], R1_04[3]);
  and and_23 (and_23_out, R0_04[4], R1_04[4]);
  and and_24 (and_24_out, R0_04[5], R1_04[5]);
  and and_25 (and_25_out, R0_04[6], R1_04[6]);
  and and_26 (and_26_out, R0_04[7], R1_04[7]);
  and and_27 (and_27_out, R0_04[8], R1_04[8]);
  and and_28 (and_28_out, R0_04[9], R1_04[9]);
  and and_29 (and_29_out, R0_04[10], R1_04[10]);
  and and_30 (and_30_out, R0_04[11], R1_04[11]);
  and and_31 (and_31_out, R0_04[12], R1_04[12]);
  and and_32 (and_32_out, R0_04[13], R1_04[13]);
  and and_33 (and_33_out, R0_04[14], R1_04[14]);
  and and_34 (and_34_out, R0_04[15], R1_04[15]);
  and and_35 (and_35_out, R0_03[0], R1_03[0]);
  and and_36 (and_36_out, R0_03[1], R1_03[1]);
  and and_37 (and_37_out, R0_03[2], R1_03[2]);
  and and_38 (and_38_out, R0_03[3], R1_03[3]);
  and and_39 (and_39_out, R0_03[4], R1_03[4]);
  and and_40 (and_40_out, R0_03[5], R1_03[5]);
  and and_41 (and_41_out, R0_03[6], R1_03[6]);
  and and_42 (and_42_out, R0_03[7], R1_03[7]);
  and and_43 (and_43_out, R0_03[8], R1_03[8]);
  and and_44 (and_44_out, R0_03[9], R1_03[9]);
  and and_45 (and_45_out, R0_03[10], R1_03[10]);
  and and_46 (and_46_out, R0_03[11], R1_03[11]);
  and and_47 (and_47_out, R0_03[12], R1_03[12]);
  and and_48 (and_48_out, R0_03[13], R1_03[13]);
  and and_49 (and_49_out, R0_03[14], R1_03[14]);
  and and_50 (and_50_out, R0_03[15], R1_03[15]);
  and and_51 (and_51_out, R0_02[0], R1_02[0]);
  and and_52 (and_52_out, R0_02[1], R1_02[1]);
  and and_53 (and_53_out, R0_02[2], R1_02[2]);
  and and_54 (and_54_out, R0_02[3], R1_02[3]);
  and and_55 (and_55_out, R0_02[4], R1_02[4]);
  and and_56 (and_56_out, R0_02[5], R1_02[5]);
  and and_57 (and_57_out, R0_02[6], R1_02[6]);
  and and_58 (and_58_out, R0_02[7], R1_02[7]);
  and and_59 (and_59_out, R0_02[8], R1_02[8]);
  and and_60 (and_60_out, R0_02[9], R1_02[9]);
  and and_61 (and_61_out, R0_02[10], R1_02[10]);
  and and_62 (and_62_out, R0_02[11], R1_02[11]);
  and and_63 (and_63_out, R0_02[12], R1_02[12]);
  and and_64 (and_64_out, R0_02[13], R1_02[13]);
  and and_65 (and_65_out, R0_02[14], R1_02[14]);
  and and_66 (and_66_out, R0_02[15], R1_02[15]);
  and and_67 (and_67_out, R0_01[0], R1_01[0]);
  and and_68 (and_68_out, R0_01[1], R1_01[1]);
  and and_69 (and_69_out, R0_01[2], R1_01[2]);
  and and_70 (and_70_out, R0_01[3], R1_01[3]);
  and and_71 (and_71_out, R0_01[4], R1_01[4]);
  and and_72 (and_72_out, R0_01[5], R1_01[5]);
  and and_73 (and_73_out, R0_01[6], R1_01[6]);
  and and_74 (and_74_out, R0_01[7], R1_01[7]);
  and and_75 (and_75_out, R0_01[8], R1_01[8]);
  and and_76 (and_76_out, R0_01[9], R1_01[9]);
  and and_77 (and_77_out, R0_01[10], R1_01[10]);
  and and_78 (and_78_out, R0_01[11], R1_01[11]);
  and and_79 (and_79_out, R0_01[12], R1_01[12]);
  and and_80 (and_80_out, R0_01[13], R1_01[13]);
  and and_81 (and_81_out, R0_01[14], R1_01[14]);
  and and_82 (and_82_out, R0_01[15], R1_01[15]);
  and and_83 (and_83_out, R0_00[0], R1_00[0]);
  and and_84 (and_84_out, R0_00[1], R1_00[1]);
  and and_85 (and_85_out, R0_00[2], R1_00[2]);
  and and_86 (and_86_out, R0_00[3], R1_00[3]);
  and and_87 (and_87_out, R0_00[4], R1_00[4]);
  and and_88 (and_88_out, R0_00[5], R1_00[5]);
  and and_89 (and_89_out, R0_00[6], R1_00[6]);
  and and_90 (and_90_out, R0_00[7], R1_00[7]);
  and and_91 (and_91_out, R0_00[8], R1_00[8]);
  and and_92 (and_92_out, R0_00[9], R1_00[9]);
  and and_93 (and_93_out, R0_00[10], R1_00[10]);
  and and_94 (and_94_out, R0_00[11], R1_00[11]);
  and and_95 (and_95_out, R0_00[12], R1_00[12]);
  and and_96 (and_96_out, R0_00[13], R1_00[13]);
  and and_97 (and_97_out, R0_00[14], R1_00[14]);
  and and_98 (and_98_out, R0_00[15], R1_00[15]);
  Multiplexer #(.width(16)) multiplexer_1 (
    .in0(shift_register_3_out), .in1(shift_register_1_out), .out(multiplexer_1_out), .sel(out_5));  // open: en
  Counter #(.max('h21), .trigger("falling")) counter_2 (
    .Q(counter_2_q), .clk(clk), .clr(out_3));  // open: load, D, count, carry
  DotMatrix #(.inputtype("row"), .matrixcols(16), .matrixrows(16)) dotmatrix_1 (
    .row0(shift_register_2_q15), .row1(shift_register_2_q14), .row2(shift_register_2_q13),
    .row3(shift_register_2_q12), .row4(shift_register_2_q11), .row5(shift_register_2_q10),
    .row6(shift_register_2_q9), .row7(shift_register_2_q8), .row8(shift_register_2_q7),
    .row9(shift_register_2_q6), .row10(shift_register_2_q5), .row11(shift_register_2_q4),
    .row12(shift_register_2_q3), .row13(shift_register_2_q2), .row14(shift_register_2_q1),
    .row15(shift_register_2_q0));
  // Probe on shift_register_3_out
  assign controlled_buffer_1_out = not_1_out ? rom_1_data : 16'bz;  // Controlled_Buffer controlled_buffer_1
  not not_1 (not_1_out, and_99_out);
  and and_99 (and_99_out, loading, primeiro_clk_32);
  Button button_1 (.out(botao1));
  Button button_2 (.out(botao2));
  or or_17 (or_17_out, and_3_out, and_4_out, and_5_out, and_6_out, and_7_out, and_8_out, and_9_out, and_10_out, and_11_out, and_12_out, and_13_out, and_14_out, and_15_out, and_16_out, and_17_out, and_18_out);
  or or_18 (or_18_out, and_19_out, and_20_out, and_21_out, and_22_out, and_23_out, and_24_out, and_25_out, and_26_out, and_27_out, and_28_out, and_29_out, and_30_out, and_31_out, and_32_out, and_33_out, and_34_out);
  or or_19 (or_19_out, and_35_out, and_36_out, and_37_out, and_38_out, and_39_out, and_40_out, and_41_out, and_42_out, and_43_out, and_44_out, and_45_out, and_46_out, and_47_out, and_48_out, and_49_out, and_50_out);
  or or_20 (or_20_out, and_51_out, and_52_out, and_53_out, and_54_out, and_55_out, and_56_out, and_57_out, and_58_out, and_59_out, and_60_out, and_61_out, and_62_out, and_63_out, and_64_out, and_65_out, and_66_out);
  or or_21 (or_21_out, and_67_out, and_68_out, and_69_out, and_70_out, and_71_out, and_72_out, and_73_out, and_74_out, and_75_out, and_76_out, and_77_out, and_78_out, and_79_out, and_80_out, and_81_out, and_82_out);
  or or_22 (or_22_out, and_83_out, and_84_out, and_85_out, and_86_out, and_87_out, and_88_out, and_89_out, and_90_out, and_91_out, and_92_out, and_93_out, and_94_out, and_95_out, and_96_out, and_97_out, and_98_out);
  Multiplexer #(.width(16)) multiplexer_2 (
    .in0(multiplexer_1_out), .in1(controlled_buffer_1_out), .out(multiplexer_2_out), .sel(not_1_out));  // open: en
  not not_2 (not_2_out, out_6);
  and and_100 (and_100_out, ~counter_2_q[0], ~counter_2_q[1], ~counter_2_q[2], ~counter_2_q[3], ~counter_2_q[4], ~counter_2_q[5], ~counter_2_q[6], ~counter_2_q[7]);  // AND_Gate
  T_Flip_Flop t_ff_3 (.clk(and_100_out), .T(1'b1), .Q(out_6));  // open: Qn, preset, reset, en
  and and_101 (out_4, ~counter_2_q[0], ~counter_2_q[1], ~counter_2_q[2], ~counter_2_q[3], counter_2_q[4], ~counter_2_q[5], ~counter_2_q[6], ~counter_2_q[7]);  // AND_Gate
  and and_102 (out_3, ~counter_2_q[0], ~counter_2_q[1], ~counter_2_q[2], ~counter_2_q[3], ~counter_2_q[4], counter_2_q[5], ~counter_2_q[6], ~counter_2_q[7]);  // AND_Gate
  and and_103 (and_103_out, ~counter_2_q[0], counter_2_q[1], ~counter_2_q[2], ~counter_2_q[3], counter_2_q[4], ~counter_2_q[5], ~counter_2_q[6], ~counter_2_q[7]);  // AND_Gate
  and and_104 (clear, counter_2_q[0], ~counter_2_q[1], ~counter_2_q[2], ~counter_2_q[3], ~counter_2_q[4], counter_2_q[5], ~counter_2_q[6], ~counter_2_q[7]);  // AND_Gate
  Multiplexer multiplexer_3 (.in0(1'b0), .in1(or_17_out), .out(multiplexer_3_out), .sel(out_4));  // open: en
  Multiplexer multiplexer_4 (.in0(1'b0), .in1(or_18_out), .out(multiplexer_4_out), .sel(out_4));  // open: en
  Multiplexer multiplexer_5 (.in0(1'b0), .in1(or_19_out), .out(multiplexer_5_out), .sel(out_4));  // open: en
  Multiplexer multiplexer_6 (.in0(1'b0), .in1(or_20_out), .out(multiplexer_6_out), .sel(out_4));  // open: en
  Multiplexer multiplexer_7 (.in0(1'b0), .in1(or_21_out), .out(multiplexer_7_out), .sel(out_4));  // open: en
  Multiplexer multiplexer_8 (.in0(1'b0), .in1(or_22_out), .out(multiplexer_8_out), .sel(out_4));  // open: en
  RAM #(.dataWidth(16), .bus("separate")) ram_1 (
    .addr(counter_2_q), .din(multiplexer_2_out), .data(ram_1_data), .str(not_2_out), .clk(clk), .ld(out_6));  // open: sel, clr
  or or_23 (or_23_out, out_4, out_3);
  or or_24 (or_24_out, and_103_out, clear);
  T_Flip_Flop t_ff_4 (.clk(or_23_out), .T(1'b1), .Q(out_5));  // open: Qn, preset, reset, en
  T_Flip_Flop t_ff_5 (.clk(or_24_out), .T(1'b1), .Q(entrada1_ON_OFF));  // open: Qn, preset, reset, en
  D_Flip_Flop d_ff_1 (.Q(primeiro_clk_16), .preset(out_4));  // open: clk, D, Qn, en, reset
  D_Flip_Flop d_ff_2 (.Q(primeiro_clk_32), .preset(out_3));  // open: clk, D, Qn, en, reset
  or or_25 (out_2, multiplexer_3_out, multiplexer_4_out, multiplexer_5_out, multiplexer_6_out, multiplexer_7_out, multiplexer_8_out);
  and and_105 (and_105_out, clk, out_6);
  Demultiplexer demultiplexer_1 (
    .out0(demultiplexer_1_out0), .out1(demultiplexer_1_out1), .in(and_105_out), .sel(out_5));  // open: en
  Demultiplexer #(.width(16)) demultiplexer_2 (
    .out0(demultiplexer_2_out0), .out1(demultiplexer_2_out1), .in(ram_1_data), .sel(out_5));  // open: en
  // Probe on L_106
  // Probe on L_107
  // Probe on L_006
  // Probe on L_007
  // Probe on L_104
  // Probe on L_105
  // Probe on L_004
  // Probe on L_005
  Shift_Register #(.width(16), .length(16)) shift_register_4 (
    .in(demultiplexer_2_out0), .clk(demultiplexer_1_out0), .q0(L_015), .q1(L_014), .q2(L_013), .q3(L_012),
    .q4(L_011), .q5(L_010), .q6(L_009), .q7(L_008), .q8(L_007), .q9(L_006), .q10(L_005), .q11(L_004),
    .q12(L_003), .q13(L_002), .q14(L_001), .q15(L_000));  // open: shift, out, load, clr, d0, d1, d2, d3, d4, d5, d6, d7, d8, d9, d10, d11, d12, d13, d14, d15
  Shift_Register #(.width(16), .length(16)) shift_register_5 (
    .in(demultiplexer_2_out1), .clk(demultiplexer_1_out1), .q0(L_115), .q1(L_114), .q2(L_113), .q3(L_112),
    .q4(L_111), .q5(L_110), .q6(L_109), .q7(L_108), .q8(L_107), .q9(L_106), .q10(L_105), .q11(L_104),
    .q12(L_103), .q13(L_102), .q14(L_101), .q15(L_100));  // open: shift, out, load, clr, d0, d1, d2, d3, d4, d5, d6, d7, d8, d9, d10, d11, d12, d13, d14, d15
  // Probe on L_102
  // Probe on L_103
  Multiplexer #(.width(16)) multiplexer_9 (
    .in0(L_115), .in1(or_26_out), .out(multiplexer_9_out), .sel(pode_atirar));  // open: en
  shift_Up_Down_16BITS shift_up_down_16bits_1 (
    ._00(L_100), ._01(L_101), ._02(L_102), ._03(L_103), ._04(L_104), ._05(L_105), ._06(L_106), ._07(L_107),
    ._08(L_108), ._09(L_109), ._10(L_110), ._11(L_111), ._12(L_112), ._13(L_113), ._14(L_114),
    ._15(multiplexer_9_out), .clk(out_6), .S_15(R0_15), .S_14(R0_14), .S_13(R0_13), .S_12(R0_12),
    .S_10(R0_10), .S_09(R0_09), .S_08(R0_08), .S_11(R0_11), .S_06(R0_06), .S_05(R0_05), .S_04(R0_04),
    .S_03(R0_03), .S_02(R0_02), .S_01(R0_01), .S_00(R0_00), .S_07(R0_07),
    .tiro_delay(shift_up_down_16bits_1_tiro_delay));
  // Probe on L_002
  // Probe on L_003
  // Probe on L_100
  // Probe on L_101
  // Probe on L_001
  // Probe on L_000
  // Probe on R0_00
  Counter #(.max('h8)) counter_3 (
    .carry(pode_atirar), .clk(shift_up_down_16bits_1_tiro_delay), .clr(and_106_out));  // open: load, D, count, Q
  and and_106 (and_106_out, pode_atirar, ~out_6);  // AND_Gate
  // Probe on R0_02
  // Probe on R0_01
  Shift_Register #(.width(16), .length(16)) shift_register_6 (
    .shift(1'b0), .clk(clk), .load(1'b1), .d15(undriven));  // open: in, out, clr, d0, q0, d1, q1, d2, q2, d3, q3, d4, q4, d5, q5, d6, q6, d7, q7, d8, q8, d9, q9, d10, q10, d11, q11, d12, q12, d13, q13, d14, q14, q15
  Random #(.width(4), .seed(91745)) random_1 (.clk(pode_atirar), .out(random_1_out));  // open: next, clr
  // Probe on R0_03
  // Probe on R0_04
  // Probe on L_000
  Decoder #(.select(4)) decoder_1 (
    .out0(decoder_1_out0[0]), .out1(decoder_1_out0[1]), .out2(decoder_1_out0[2]), .out3(decoder_1_out0[3]),
    .out4(decoder_1_out0[4]), .out5(decoder_1_out0[5]), .out6(decoder_1_out0[6]), .out7(decoder_1_out0[7]),
    .out8(decoder_1_out0[8]), .out9(decoder_1_out0[9]), .out10(decoder_1_out0[10]),
    .out11(decoder_1_out0[11]), .out12(decoder_1_out0[12]), .out13(decoder_1_out0[13]),
    .out14(decoder_1_out0[14]), .out15(decoder_1_out0[15]), .sel(random_1_out));  // open: en
  // Probe on R0_05
  // Probe on R0_06
  // Probe on L_001
  // Probe on L_002
  Random #(.width(4), .seed(5491276)) random_2 (.clk(pode_atirar), .out(random_2_out));  // open: next, clr
  // Probe on R0_07
  // Probe on R0_08
  // Probe on L_003
  // Probe on L_004
  assign or_26_out = decoder_1_out0 | decoder_2_out0;  // OR_Gate or_26, 16 bits wide
  Decoder #(.select(4)) decoder_2 (
    .out0(decoder_2_out0[0]), .out1(decoder_2_out0[1]), .out2(decoder_2_out0[2]), .out3(decoder_2_out0[3]),
    .out4(decoder_2_out0[4]), .out5(decoder_2_out0[5]), .out6(decoder_2_out0[6]), .out7(decoder_2_out0[7]),
    .out8(decoder_2_out0[8]), .out9(decoder_2_out0[9]), .out10(decoder_2_out0[10]),
    .out11(decoder_2_out0[11]), .out12(decoder_2_out0[12]), .out13(decoder_2_out0[13]),
    .out14(decoder_2_out0[14]), .out15(decoder_2_out0[15]), .sel(random_2_out));  // open: en
  // Probe on R0_10
  // Probe on R0_09
  // Probe on L_005
  // Probe on L_006
  // Probe on R0_12
  // Probe on R0_11
  // Probe on L_008
  // Probe on L_007
  shift_Left_Right_16BITS shift_left_right_16bits_1 (
    .botao1(botao1), .botao2(botao2), .L_015(R1_15), .L_007(R1_07), .L_014(R1_14), .L_006(R1_06),
    .L_013(R1_13), .L_005(R1_05), .L_012(R1_12), .L_004(R1_04), .L_011(R1_11), .L_003(R1_03), .L_010(R1_10),
    .L_002(R1_02), .L_009(R1_09), .L_001(R1_01), .L_008(R1_08), .L_000(R1_00), ._01(L_001), ._02(L_002),
    ._03(L_003), ._04(L_004), ._05(L_005), ._06(L_006), ._07(L_007), ._08(L_008), ._09(L_009), ._10(L_010),
    ._11(L_011), ._12(L_012), ._13(L_013), ._14(L_014), ._15(L_015), ._00(L_000));
  // Probe on R1_00
  // Probe on R1_00
  // Probe on R0_14
  // Probe on R0_13
  // Probe on L_010
  // Probe on L_009
  // Probe on R1_01
  // Probe on R1_02
  // Probe on R1_02
  // Probe on R1_01
  // Probe on R0_15
  // Probe on L_011
  // Probe on L_012
  // Probe on R1_03
  // Probe on R1_04
  // Probe on R1_04
  // Probe on R1_03
  // Probe on L_014
  // Probe on L_013
  // Probe on R1_06
  // Probe on R1_05
  // Probe on R1_05
  // Probe on R1_06
  // Probe on L_015
  // Probe on R1_08
  // Probe on R1_07
  // Probe on R1_07
  // Probe on R1_08
  // Probe on R1_09
  // Probe on R1_10
  // Probe on R1_10
  // Probe on R1_09
  // Probe on R1_11
  // Probe on R1_12
  // Probe on R1_12
  // Probe on R1_11
  // Probe on R1_13
  // Probe on R1_14
  // Probe on R1_13
  // Probe on R1_14
  // Probe on R1_15
  // Probe on R1_15

  // Other names for the same wires on the sheet: clk_16 = out_4; clk_32 = out_3; E_S = out_6; perdeu = out_2;
  //   rota = out_5

  // Notes on the sheet:
  //   ROM
  //   contents of rom_1 (hex, n*v repeats v):
  //   0 1c0 80 80 3e0 80
endmodule

module shift_Left_Right_16BITS (
  input  [15:0] _00,
  input  [15:0] _01,
  input  [15:0] _02,
  input  [15:0] _03,
  input  [15:0] _04,
  input  [15:0] _05,
  input  [15:0] _06,
  input  [15:0] _07,
  input  [15:0] _08,
  input  [15:0] _09,
  input  [15:0] _10,
  input  [15:0] _11,
  input  [15:0] _12,
  input  [15:0] _13,
  input  [15:0] _14,
  input  [15:0] _15,
  input  botao1,
  input  botao2,
  output [15:0] L_015,
  output [15:0] L_007,
  output [15:0] L_014,
  output [15:0] L_006,
  output [15:0] L_013,
  output [15:0] L_005,
  output [15:0] L_012,
  output [15:0] L_004,
  output [15:0] L_011,
  output [15:0] L_003,
  output [15:0] L_010,
  output [15:0] L_002,
  output [15:0] L_009,
  output [15:0] L_001,
  output [15:0] L_008,
  output [15:0] L_000
);

  wire comparator_1_eq, comparator_1_gt, comparator_2_eq, comparator_2_gt, not_1_out, not_2_out, or_1_out,
       or_2_out;
  wire [1:0] rota;
  wire [15:0] demultiplexer_1_out0, demultiplexer_1_out1, demultiplexer_1_out2, demultiplexer_2_out0,
       demultiplexer_2_out1, demultiplexer_2_out2, demultiplexer_3_out0, demultiplexer_3_out1,
       demultiplexer_3_out2, demultiplexer_4_out0, demultiplexer_4_out1, demultiplexer_4_out2,
       demultiplexer_5_out0, demultiplexer_5_out1, demultiplexer_5_out2, demultiplexer_6_out0,
       demultiplexer_6_out1, demultiplexer_6_out2, demultiplexer_7_out0, demultiplexer_7_out1,
       demultiplexer_7_out2, demultiplexer_8_out0, demultiplexer_8_out1, demultiplexer_8_out2,
       demultiplexer_9_out0, demultiplexer_9_out1, demultiplexer_9_out2, demultiplexer_10_out0,
       demultiplexer_10_out1, demultiplexer_10_out2, demultiplexer_11_out0, demultiplexer_11_out1,
       demultiplexer_11_out2, demultiplexer_12_out0, demultiplexer_12_out1, demultiplexer_12_out2,
       demultiplexer_13_out0, demultiplexer_13_out1, demultiplexer_13_out2, demultiplexer_14_out0,
       demultiplexer_14_out1, demultiplexer_14_out2, demultiplexer_15_out0, demultiplexer_15_out1,
       demultiplexer_15_out2, demultiplexer_16_out0, demultiplexer_16_out1, demultiplexer_16_out2,
       shifter_1_out, shifter_2_out, shifter_3_out, shifter_4_out, shifter_5_out, shifter_6_out,
       shifter_7_out, shifter_8_out, shifter_9_out, shifter_10_out, shifter_11_out, shifter_12_out,
       shifter_13_out, shifter_14_out, shifter_15_out, shifter_16_out, shifter_17_out, shifter_18_out,
       shifter_19_out, shifter_20_out, shifter_21_out, shifter_22_out, shifter_23_out, shifter_24_out,
       shifter_25_out, shifter_26_out, shifter_27_out, shifter_28_out, shifter_29_out, shifter_30_out,
       shifter_31_out, shifter_32_out;

  Comparator #(.width(16)) comparator_1 (
    .a(_04), .b(16'hf800), .gt(comparator_1_gt), .eq(comparator_1_eq));  // open: lt
  Comparator #(.width(16)) comparator_2 (.a(_04), .b(16'h1f), .gt(comparator_2_gt), .eq(comparator_2_eq));  // open: lt
  or or_1 (or_1_out, comparator_1_gt, comparator_2_eq);
  not not_1 (not_1_out, botao2);
  not not_2 (not_2_out, botao1);
  or or_2 (or_2_out, comparator_2_gt, comparator_1_eq);
  and and_1 (rota[0], or_1_out, botao1, not_1_out);
  and and_2 (rota[1], not_2_out, botao2, or_2_out);
  Demultiplexer #(.select(2), .width(16)) demultiplexer_1 (
    .out0(demultiplexer_1_out0), .out1(demultiplexer_1_out1), .out2(demultiplexer_1_out2), .in(_15),
    .sel(rota));  // open: out3, en
  Demultiplexer #(.select(2), .width(16)) demultiplexer_2 (
    .out0(demultiplexer_2_out0), .out1(demultiplexer_2_out1), .out2(demultiplexer_2_out2), .in(_14),
    .sel(rota));  // open: out3, en
  Demultiplexer #(.select(2), .width(16)) demultiplexer_3 (
    .out0(demultiplexer_3_out0), .out1(demultiplexer_3_out1), .out2(demultiplexer_3_out2), .in(_13),
    .sel(rota));  // open: out3, en
  Demultiplexer #(.select(2), .width(16)) demultiplexer_4 (
    .out0(demultiplexer_4_out0), .out1(demultiplexer_4_out1), .out2(demultiplexer_4_out2), .in(_12),
    .sel(rota));  // open: out3, en
  Demultiplexer #(.select(2), .width(16)) demultiplexer_5 (
    .out0(demultiplexer_5_out0), .out1(demultiplexer_5_out1), .out2(demultiplexer_5_out2), .in(_11),
    .sel(rota));  // open: out3, en
  Demultiplexer #(.select(2), .width(16)) demultiplexer_6 (
    .out0(demultiplexer_6_out0), .out1(demultiplexer_6_out1), .out2(demultiplexer_6_out2), .in(_10),
    .sel(rota));  // open: out3, en
  Demultiplexer #(.select(2), .width(16)) demultiplexer_7 (
    .out0(demultiplexer_7_out0), .out1(demultiplexer_7_out1), .out2(demultiplexer_7_out2), .in(_09),
    .sel(rota));  // open: out3, en
  Demultiplexer #(.select(2), .width(16)) demultiplexer_8 (
    .out0(demultiplexer_8_out0), .out1(demultiplexer_8_out1), .out2(demultiplexer_8_out2), .in(_08),
    .sel(rota));  // open: out3, en
  Shifter #(.width(16)) shifter_1 (.in(demultiplexer_1_out1), .\dist (4'b0001), .out(shifter_1_out));
  Shifter #(.width(16), .shift("lr")) shifter_2 (.in(demultiplexer_1_out2), .\dist (4'b0001), .out(shifter_2_out));
  Shifter #(.width(16)) shifter_3 (.in(demultiplexer_2_out1), .\dist (4'b0001), .out(shifter_3_out));
  Shifter #(.width(16), .shift("lr")) shifter_4 (.in(demultiplexer_2_out2), .\dist (4'b0001), .out(shifter_4_out));
  Shifter #(.width(16)) shifter_5 (.in(demultiplexer_3_out1), .\dist (4'b0001), .out(shifter_5_out));
  Shifter #(.width(16), .shift("lr")) shifter_6 (.in(demultiplexer_3_out2), .\dist (4'b0001), .out(shifter_6_out));
  Shifter #(.width(16)) shifter_7 (.in(demultiplexer_4_out1), .\dist (4'b0001), .out(shifter_7_out));
  Shifter #(.width(16), .shift("lr")) shifter_8 (.in(demultiplexer_4_out2), .\dist (4'b0001), .out(shifter_8_out));
  Shifter #(.width(16)) shifter_9 (.in(demultiplexer_5_out1), .\dist (4'b0001), .out(shifter_9_out));
  Shifter #(.width(16), .shift("lr")) shifter_10 (.in(demultiplexer_5_out2), .\dist (4'b0001), .out(shifter_10_out));
  Shifter #(.width(16)) shifter_11 (.in(demultiplexer_6_out1), .\dist (4'b0001), .out(shifter_11_out));
  Shifter #(.width(16), .shift("lr")) shifter_12 (.in(demultiplexer_6_out2), .\dist (4'b0001), .out(shifter_12_out));
  Shifter #(.width(16)) shifter_13 (.in(demultiplexer_7_out1), .\dist (4'b0001), .out(shifter_13_out));
  Shifter #(.width(16), .shift("lr")) shifter_14 (.in(demultiplexer_7_out2), .\dist (4'b0001), .out(shifter_14_out));
  Shifter #(.width(16)) shifter_15 (.in(demultiplexer_8_out1), .\dist (4'b0001), .out(shifter_15_out));
  Shifter #(.width(16), .shift("lr")) shifter_16 (.in(demultiplexer_8_out2), .\dist (4'b0001), .out(shifter_16_out));
  assign L_015 = demultiplexer_1_out0 | shifter_1_out | shifter_2_out;  // OR_Gate or_3, 16 bits wide
  assign L_014 = demultiplexer_2_out0 | shifter_3_out | shifter_4_out;  // OR_Gate or_4, 16 bits wide
  assign L_013 = demultiplexer_3_out0 | shifter_5_out | shifter_6_out;  // OR_Gate or_5, 16 bits wide
  assign L_012 = demultiplexer_4_out0 | shifter_7_out | shifter_8_out;  // OR_Gate or_6, 16 bits wide
  assign L_011 = demultiplexer_5_out0 | shifter_9_out | shifter_10_out;  // OR_Gate or_7, 16 bits wide
  assign L_010 = demultiplexer_6_out0 | shifter_11_out | shifter_12_out;  // OR_Gate or_8, 16 bits wide
  assign L_009 = demultiplexer_7_out0 | shifter_13_out | shifter_14_out;  // OR_Gate or_9, 16 bits wide
  assign L_008 = demultiplexer_8_out0 | shifter_15_out | shifter_16_out;  // OR_Gate or_10, 16 bits wide
  Demultiplexer #(.select(2), .width(16)) demultiplexer_9 (
    .out0(demultiplexer_9_out0), .out1(demultiplexer_9_out1), .out2(demultiplexer_9_out2), .in(_07),
    .sel(rota));  // open: out3, en
  Demultiplexer #(.select(2), .width(16)) demultiplexer_10 (
    .out0(demultiplexer_10_out0), .out1(demultiplexer_10_out1), .out2(demultiplexer_10_out2), .in(_06),
    .sel(rota));  // open: out3, en
  Demultiplexer #(.select(2), .width(16)) demultiplexer_11 (
    .out0(demultiplexer_11_out0), .out1(demultiplexer_11_out1), .out2(demultiplexer_11_out2), .in(_05),
    .sel(rota));  // open: out3, en
  Demultiplexer #(.select(2), .width(16)) demultiplexer_12 (
    .out0(demultiplexer_12_out0), .out1(demultiplexer_12_out1), .out2(demultiplexer_12_out2), .in(_04),
    .sel(rota));  // open: out3, en
  Demultiplexer #(.select(2), .width(16)) demultiplexer_13 (
    .out0(demultiplexer_13_out0), .out1(demultiplexer_13_out1), .out2(demultiplexer_13_out2), .in(_03),
    .sel(rota));  // open: out3, en
  Demultiplexer #(.select(2), .width(16)) demultiplexer_14 (
    .out0(demultiplexer_14_out0), .out1(demultiplexer_14_out1), .out2(demultiplexer_14_out2), .in(_02),
    .sel(rota));  // open: out3, en
  Demultiplexer #(.select(2), .width(16)) demultiplexer_15 (
    .out0(demultiplexer_15_out0), .out1(demultiplexer_15_out1), .out2(demultiplexer_15_out2), .in(_01),
    .sel(rota));  // open: out3, en
  Demultiplexer #(.select(2), .width(16)) demultiplexer_16 (
    .out0(demultiplexer_16_out0), .out1(demultiplexer_16_out1), .out2(demultiplexer_16_out2), .in(_00),
    .sel(rota));  // open: out3, en
  Shifter #(.width(16)) shifter_17 (.in(demultiplexer_9_out1), .\dist (4'b0001), .out(shifter_17_out));
  Shifter #(.width(16), .shift("lr")) shifter_18 (.in(demultiplexer_9_out2), .\dist (4'b0001), .out(shifter_18_out));
  Shifter #(.width(16)) shifter_19 (.in(demultiplexer_10_out1), .\dist (4'b0001), .out(shifter_19_out));
  Shifter #(.width(16), .shift("lr")) shifter_20 (.in(demultiplexer_10_out2), .\dist (4'b0001), .out(shifter_20_out));
  Shifter #(.width(16)) shifter_21 (.in(demultiplexer_11_out1), .\dist (4'b0001), .out(shifter_21_out));
  Shifter #(.width(16), .shift("lr")) shifter_22 (.in(demultiplexer_11_out2), .\dist (4'b0001), .out(shifter_22_out));
  Shifter #(.width(16)) shifter_23 (.in(demultiplexer_12_out1), .\dist (4'b0001), .out(shifter_23_out));
  Shifter #(.width(16), .shift("lr")) shifter_24 (.in(demultiplexer_12_out2), .\dist (4'b0001), .out(shifter_24_out));
  Shifter #(.width(16)) shifter_25 (.in(demultiplexer_13_out1), .\dist (4'b0001), .out(shifter_25_out));
  Shifter #(.width(16), .shift("lr")) shifter_26 (.in(demultiplexer_13_out2), .\dist (4'b0001), .out(shifter_26_out));
  Shifter #(.width(16)) shifter_27 (.in(demultiplexer_14_out1), .\dist (4'b0001), .out(shifter_27_out));
  Shifter #(.width(16), .shift("lr")) shifter_28 (.in(demultiplexer_14_out2), .\dist (4'b0001), .out(shifter_28_out));
  Shifter #(.width(16)) shifter_29 (.in(demultiplexer_15_out1), .\dist (4'b0001), .out(shifter_29_out));
  Shifter #(.width(16), .shift("lr")) shifter_30 (.in(demultiplexer_15_out2), .\dist (4'b0001), .out(shifter_30_out));
  Shifter #(.width(16)) shifter_31 (.in(demultiplexer_16_out1), .\dist (4'b0001), .out(shifter_31_out));
  Shifter #(.width(16), .shift("lr")) shifter_32 (.in(demultiplexer_16_out2), .\dist (4'b0001), .out(shifter_32_out));
  assign L_007 = demultiplexer_9_out0 | shifter_17_out | shifter_18_out;  // OR_Gate or_11, 16 bits wide
  assign L_006 = demultiplexer_10_out0 | shifter_19_out | shifter_20_out;  // OR_Gate or_12, 16 bits wide
  assign L_005 = demultiplexer_11_out0 | shifter_21_out | shifter_22_out;  // OR_Gate or_13, 16 bits wide
  assign L_004 = demultiplexer_12_out0 | shifter_23_out | shifter_24_out;  // OR_Gate or_14, 16 bits wide
  assign L_003 = demultiplexer_13_out0 | shifter_25_out | shifter_26_out;  // OR_Gate or_15, 16 bits wide
  assign L_002 = demultiplexer_14_out0 | shifter_27_out | shifter_28_out;  // OR_Gate or_16, 16 bits wide
  assign L_001 = demultiplexer_15_out0 | shifter_29_out | shifter_30_out;  // OR_Gate or_17, 16 bits wide
  assign L_000 = demultiplexer_16_out0 | shifter_31_out | shifter_32_out;  // OR_Gate or_18, 16 bits wide

  // Other names for the same wires on the sheet: L_000_t[15:0] = _00; L_001_t[15:0] = _01; L_002_t[15:0] = _02;
  //   L_003_t[15:0] = _03; L_004_t[15:0] = _04; L_005_t[15:0] = _05; L_006_t[15:0] = _06; L_007_t[15:0] = _07;
  //   L_008_t[15:0] = _08; L_009_t[15:0] = _09; L_010_t[15:0] = _10; L_011_t[15:0] = _11; L_012_t[15:0] = _12;
  //   L_013_t[15:0] = _13; L_014_t[15:0] = _14; L_015_t[15:0] = _15
endmodule

module shift_Up_Down_16BITS (
  input  [15:0] _00,
  input  [15:0] _01,
  input  [15:0] _02,
  input  [15:0] _03,
  input  [15:0] _04,
  input  [15:0] _05,
  input  [15:0] _06,
  input  [15:0] _07,
  input  [15:0] _08,
  input  [15:0] _09,
  input  [15:0] _10,
  input  [15:0] _11,
  input  [15:0] _12,
  input  [15:0] _13,
  input  [15:0] _14,
  input  [15:0] _15,
  input  clk,
  output [15:0] S_15,
  output tiro_delay,
  output [15:0] S_14,
  output [15:0] S_13,
  output [15:0] S_12,
  output [15:0] S_11,
  output [15:0] S_10,
  output [15:0] S_09,
  output [15:0] S_08,
  output [15:0] S_07,
  output [15:0] S_06,
  output [15:0] S_05,
  output [15:0] S_04,
  output [15:0] S_03,
  output [15:0] S_02,
  output [15:0] S_01,
  output [15:0] S_00
);

  wire [15:0] demultiplexer_1_out1, demultiplexer_2_out0, demultiplexer_2_out1, demultiplexer_3_out0,
       demultiplexer_3_out1, demultiplexer_4_out0, demultiplexer_4_out1, demultiplexer_5_out0,
       demultiplexer_5_out1, demultiplexer_6_out0, demultiplexer_6_out1, demultiplexer_7_out0,
       demultiplexer_7_out1, demultiplexer_8_out0, demultiplexer_8_out1, demultiplexer_9_out0,
       demultiplexer_9_out1, demultiplexer_10_out0, demultiplexer_10_out1, demultiplexer_11_out0,
       demultiplexer_11_out1, demultiplexer_12_out0, demultiplexer_12_out1, demultiplexer_13_out0,
       demultiplexer_13_out1, demultiplexer_14_out0, demultiplexer_14_out1, demultiplexer_15_out0,
       demultiplexer_15_out1, demultiplexer_16_out0;

  Counter #(.max('h2)) counter_1 (.carry(tiro_delay), .clk(clk));  // open: load, D, count, Q, clr
  Demultiplexer #(.width(16)) demultiplexer_1 (
    .out0(S_15), .out1(demultiplexer_1_out1), .in(_15), .sel(tiro_delay));  // open: en
  Demultiplexer #(.width(16)) demultiplexer_2 (
    .out0(demultiplexer_2_out0), .out1(demultiplexer_2_out1), .in(_14), .sel(tiro_delay));  // open: en
  Demultiplexer #(.width(16)) demultiplexer_3 (
    .out0(demultiplexer_3_out0), .out1(demultiplexer_3_out1), .in(_13), .sel(tiro_delay));  // open: en
  Demultiplexer #(.width(16)) demultiplexer_4 (
    .out0(demultiplexer_4_out0), .out1(demultiplexer_4_out1), .in(_12), .sel(tiro_delay));  // open: en
  Demultiplexer #(.width(16)) demultiplexer_5 (
    .out0(demultiplexer_5_out0), .out1(demultiplexer_5_out1), .in(_11), .sel(tiro_delay));  // open: en
  Demultiplexer #(.width(16)) demultiplexer_6 (
    .out0(demultiplexer_6_out0), .out1(demultiplexer_6_out1), .in(_10), .sel(tiro_delay));  // open: en
  Demultiplexer #(.width(16)) demultiplexer_7 (
    .out0(demultiplexer_7_out0), .out1(demultiplexer_7_out1), .in(_09), .sel(tiro_delay));  // open: en
  Demultiplexer #(.width(16)) demultiplexer_8 (
    .out0(demultiplexer_8_out0), .out1(demultiplexer_8_out1), .in(_08), .sel(tiro_delay));  // open: en
  Demultiplexer #(.width(16)) demultiplexer_9 (
    .out0(demultiplexer_9_out0), .out1(demultiplexer_9_out1), .in(_07), .sel(tiro_delay));  // open: en
  Demultiplexer #(.width(16)) demultiplexer_10 (
    .out0(demultiplexer_10_out0), .out1(demultiplexer_10_out1), .in(_06), .sel(tiro_delay));  // open: en
  Demultiplexer #(.width(16)) demultiplexer_11 (
    .out0(demultiplexer_11_out0), .out1(demultiplexer_11_out1), .in(_05), .sel(tiro_delay));  // open: en
  Demultiplexer #(.width(16)) demultiplexer_12 (
    .out0(demultiplexer_12_out0), .out1(demultiplexer_12_out1), .in(_04), .sel(tiro_delay));  // open: en
  Demultiplexer #(.width(16)) demultiplexer_13 (
    .out0(demultiplexer_13_out0), .out1(demultiplexer_13_out1), .in(_03), .sel(tiro_delay));  // open: en
  Demultiplexer #(.width(16)) demultiplexer_14 (
    .out0(demultiplexer_14_out0), .out1(demultiplexer_14_out1), .in(_02), .sel(tiro_delay));  // open: en
  Demultiplexer #(.width(16)) demultiplexer_15 (
    .out0(demultiplexer_15_out0), .out1(demultiplexer_15_out1), .in(_01), .sel(tiro_delay));  // open: en
  Demultiplexer #(.width(16)) demultiplexer_16 (
    .out0(demultiplexer_16_out0), .in(_00), .sel(tiro_delay));  // open: out1, en
  assign S_14 = demultiplexer_1_out1 | demultiplexer_2_out0;  // OR_Gate or_1, 16 bits wide
  assign S_13 = demultiplexer_2_out1 | demultiplexer_3_out0;  // OR_Gate or_2, 16 bits wide
  assign S_12 = demultiplexer_3_out1 | demultiplexer_4_out0;  // OR_Gate or_3, 16 bits wide
  assign S_11 = demultiplexer_4_out1 | demultiplexer_5_out0;  // OR_Gate or_4, 16 bits wide
  assign S_10 = demultiplexer_5_out1 | demultiplexer_6_out0;  // OR_Gate or_5, 16 bits wide
  assign S_09 = demultiplexer_6_out1 | demultiplexer_7_out0;  // OR_Gate or_6, 16 bits wide
  assign S_08 = demultiplexer_7_out1 | demultiplexer_8_out0;  // OR_Gate or_7, 16 bits wide
  assign S_07 = demultiplexer_8_out1 | demultiplexer_9_out0;  // OR_Gate or_8, 16 bits wide
  assign S_06 = demultiplexer_9_out1 | demultiplexer_10_out0;  // OR_Gate or_9, 16 bits wide
  assign S_05 = demultiplexer_10_out1 | demultiplexer_11_out0;  // OR_Gate or_10, 16 bits wide
  assign S_04 = demultiplexer_11_out1 | demultiplexer_12_out0;  // OR_Gate or_11, 16 bits wide
  assign S_03 = demultiplexer_12_out1 | demultiplexer_13_out0;  // OR_Gate or_12, 16 bits wide
  assign S_02 = demultiplexer_13_out1 | demultiplexer_14_out0;  // OR_Gate or_13, 16 bits wide
  assign S_01 = demultiplexer_14_out1 | demultiplexer_15_out0;  // OR_Gate or_14, 16 bits wide
  assign S_00 = demultiplexer_15_out1 | demultiplexer_16_out0;  // OR_Gate or_15, 16 bits wide

  // Other names for the same wires on the sheet: L_000[15:0] = _00; L_001[15:0] = _01; L_002[15:0] = _02;
  //   L_003[15:0] = _03; L_004[15:0] = _04; L_005[15:0] = _05; L_006[15:0] = _06; L_007[15:0] = _07;
  //   L_008[15:0] = _08; L_009[15:0] = _09; L_010[15:0] = _10; L_011[15:0] = _11; L_012[15:0] = _12;
  //   L_013[15:0] = _13; L_014[15:0] = _14; L_015[15:0] = _15; rota = tiro_delay
endmodule
